# Fritzing sketch board-water-meter-monitor (saved by Fritzing 0.9.3b)
perfboards: 1

parts:
  U3 = NodeMCU V3.0
  RHT1 = Humidity and Temperature Sensor RHT03  # not connected
  Part1 = Barometric Pressure Sensor - BMP180 Breakout (GY-68)  # not connected
  Part2 = Analog Digital MUX Breakout
  M1 = fc-51 [package=THT]  # not connected
  M2 = fc-51 [package=THT]  # not connected
  J2 = female pin header, 3 pins [form="♀ (female)"]
  J3 = female pin header, 4 pins [form="♀ (female)"]
  J4 = female pin header, 15 pins [form="♀ (female)"]
  J5 = female pin header, 15 pins [form="♀ (female)"]
  J1 = female pin header, 8 pins [form="♀ (female)"]
  J6 = female pin header, 16 pins [form="♀ (female)"]
  J7 = female pin header, 3 pins [form="♀ (female)"]  # not connected
  J8 = female pin header, 3 pins [form="♀ (female)"]

nets:
  N1: U3.GND#6, U3.GND#13, U3.GND#16, U3.GND#33
  N2: Part2.C0, J6.pin16
  N3: Part2.C1, J6.pin15
  N4: Part2.C2, J6.pin14
  N5: Part2.C3, J6.pin13
  N6: Part2.C4, J6.pin12
  N7: Part2.C5, J6.pin11
  N8: Part2.C6, J6.pin10
  N9: Part2.C7, J6.pin9
  N10: Part2.C8, J6.pin8
  N11: Part2.C9, J6.pin7
  N12: Part2.C10, J6.pin6
  N13: Part2.C11, J6.pin5
  N14: Part2.C12, J6.pin4
  N15: Part2.C13, J6.pin3
  N16: Part2.C14, J6.pin2
  N17: Part2.C15, J6.pin1
  N18: J2.pin2, J5.pin7
  N19: J3.pin3, J5.pin14
  N20: J3.pin4, J5.pin13
  N21: J4.pin15, J1.pin1
  N22: J5.pin5, J1.pin5
  N23: J5.pin6, J1.pin4
  N24: J5.pin11, J1.pin2
  N25: J5.pin12, J1.pin3
  N26: J1.pin7, J8.pin1

notes:
  COLD
  HOT
  BMP180
  DT22
  GND bus
  3V bus

custom parts:
  NodeMCU V3.0: ESP8266 based NodeMCU
