# Fritzing sketch dht22_bmp180_onNodeMCU (saved by Fritzing 0.9.3b)

parts:
  U3 = NodeMCU V3.0
  RHT1 = Humidity and Temperature Sensor RHT03
  Part1 = Barometric Pressure Sensor - BMP180 Breakout (GY-68)

nets:
  N1: U3.D1, Part1.SCL
  N2: U3.D2, Part1.SDA
  VCC: U3.3V3, RHT1.Vcc, Part1.VCC
  GND: U3.GND, RHT1.GND_2, Part1.GND
  N3: U3.D6, RHT1.Data-signal

custom parts:
  NodeMCU V3.0: ESP8266 based NodeMCU
