# Fritzing sketch multiplexer (saved by Fritzing 0.9.3b)

parts:
  U3 = NodeMCU V3.0
  Part2 = Analog Digital MUX Breakout

nets:
  N1: U3.D3, Part2.S2
  N2: U3.D4, Part2.S3
  3V3: U3.3V3, Part2.VCC
  N3: U3.D7, Part2.S0
  N4: U3.D8, Part2.S1
  GND: U3.GND, Part2.GND, Part2.EN
  N5: U3.A0, Part2.SIG

custom parts:
  NodeMCU V3.0: ESP8266 based NodeMCU
