# Fritzing sketch reflectance_sensors (saved by Fritzing 0.9.3b)

parts:
  U3 = NodeMCU V3.0
  Part2 = Analog Digital MUX Breakout
  M1 = fc-51 [package=THT]
  M2 = fc-51 [package=THT]

nets:
  N1: U3.D3, Part2.S2
  N2: U3.D4, Part2.S3
  3V3: U3.3V3, Part2.VCC, M1.pin3, M2.pin3
  N3: U3.D7, Part2.S0
  N4: U3.D8, Part2.S1
  GND: U3.GND, Part2.GND, Part2.EN, M1.pin2, M2.pin2
  N5: U3.A0, Part2.SIG
  N6: Part2.C0, M2.pin1
  N7: Part2.C1, M1.pin1

custom parts:
  NodeMCU V3.0: ESP8266 based NodeMCU
