# Fritzing sketch test-with-nano (saved by Fritzing 0.9.3b)

parts:
  Part1 = Arduino Nano (Rev3.0)
  RHT1 = Humidity and Temperature Sensor RHT03

nets:
  N1: Part1.D12/MISO, RHT1.Data-signal
  N2: Part1.GND, RHT1.GND_2
  3V3: Part1.3V3, RHT1.Vcc
