# Fritzing sketch water-meter-monitor (saved by Fritzing 0.9.3b)

parts:
  U3 = NodeMCU V3.0
  RHT1 = Humidity and Temperature Sensor RHT03
  Part1 = Barometric Pressure Sensor - BMP180 Breakout (GY-68)
  Part2 = Analog Digital MUX Breakout
  M1 = fc-51 [package=THT]
  M2 = fc-51 [package=THT]

nets:
  N1: U3.D1, Part1.SCL
  N2: U3.D2, Part1.SDA
  N3: U3.D3, Part2.S2
  N4: U3.D4, Part2.S3
  VCC: U3.3V3, RHT1.Vcc, Part1.VCC, Part2.VCC, M1.pin3, M2.pin3
  N5: U3.GND#6, U3.GND#13, U3.GND#16, RHT1.GND_2, Part1.GND
  N6: U3.D6, RHT1.Data-signal
  N7: U3.D7, Part2.S1
  N8: U3.D8, Part2.S0
  N9: U3.GND#41, Part2.GND, Part2.EN, M1.pin2, M2.pin2
  N10: U3.A0, Part2.SIG
  N11: Part2.C0, M2.pin1
  N12: Part2.C1, M1.pin1

custom parts:
  NodeMCU V3.0: ESP8266 based NodeMCU
